// Logisim project registers.circ as structural Verilog: 1 circuit, main circuit registers
module registers (
  input  [7:0] data,
  input  write,
  input  [1:0] \reg ,
  input  clear,
  output [7:0] a,
  output [7:0] b,
  output [7:0] out,
  output [7:0] mbr
);

  wire demultiplexer_1_out0, demultiplexer_1_out1, demultiplexer_1_out2, demultiplexer_1_out3;

  Demultiplexer #(.select(2), .enable("false")) demultiplexer_1 (
    .out0(demultiplexer_1_out0), .out1(demultiplexer_1_out1), .out2(demultiplexer_1_out2),
    .out3(demultiplexer_1_out3), .in(write), .sel(\reg ));
  Register u_A (.D(data), .Q(a), .clk(demultiplexer_1_out0), .clr(clear));  // open: en
  Register u_B (.D(data), .Q(b), .clk(demultiplexer_1_out1), .clr(clear));  // open: en
  Register u_OUT (.D(data), .Q(out), .clk(demultiplexer_1_out2), .clr(clear));  // open: en
  Register u_MBR (.D(data), .Q(mbr), .clk(demultiplexer_1_out3), .clr(clear));  // open: en
endmodule
